// Logisim project Лаба 2.circ as structural Verilog: 1 circuit, main circuit main
module main (
  input  \НЕ ,
  input  \И ,
  input  in_3,
  input  \ИЛИ ,
  input  in_5,
  input  \ИЛИ_НЕ ,
  input  in_7,
  input  \И_НЕ ,
  input  in_9,
  output out_10,
  output out_11,
  output out_12,
  output out_13,
  output out_14
);

  wire transistor_3_out, transistor_10_out, transistor_14_out, transistor_18_out;

  Transistor transistor_1 (.in(1'b1), .out(out_10), .gate(\НЕ ));
  Transistor #(.\type ("n")) transistor_2 (.in(1'b0), .out(out_10), .gate(\НЕ ));
  Transistor #(.\type ("n")) transistor_3 (.in(1'b1), .out(transistor_3_out), .gate(\И ));
  Transistor #(.\type ("n")) transistor_4 (.in(transistor_3_out), .out(out_11), .gate(in_3));
  Transistor transistor_5 (.in(1'b0), .out(out_11), .gate(\И ));
  Transistor transistor_6 (.in(1'b0), .out(out_11), .gate(in_3));
  Transistor #(.\type ("n")) transistor_7 (.in(1'b1), .out(out_12), .gate(in_5));
  Transistor #(.\type ("n")) transistor_8 (.in(1'b1), .out(out_12), .gate(\ИЛИ ));
  Transistor transistor_9 (.in(transistor_10_out), .out(out_12), .gate(in_5));
  Transistor transistor_10 (.in(1'b0), .out(transistor_10_out), .gate(\ИЛИ ));
  Transistor #(.\type ("n")) transistor_11 (.in(1'b0), .out(out_13), .gate(in_7));
  Transistor #(.\type ("n")) transistor_12 (.in(1'b0), .out(out_13), .gate(\ИЛИ_НЕ ));
  Transistor transistor_13 (.in(transistor_14_out), .out(out_13), .gate(in_7));
  Transistor transistor_14 (.in(1'b1), .out(transistor_14_out), .gate(\ИЛИ_НЕ ));
  Transistor transistor_15 (.in(1'b1), .out(out_14), .gate(in_9));
  Transistor transistor_16 (.in(1'b1), .out(out_14), .gate(\И_НЕ ));
  Transistor #(.\type ("n")) transistor_17 (.in(transistor_18_out), .out(out_14), .gate(in_9));
  Transistor #(.\type ("n")) transistor_18 (.in(1'b0), .out(transistor_18_out), .gate(\И_НЕ ));
endmodule
