// Logisim project 4 ЛАБА.circ as structural Verilog
module encoder (
  input  _0,
  input  _1,
  input  _2,
  input  _3,
  input  _4,
  input  _5,
  input  _6,
  input  _7,
  input  _8,
  input  _9,
  input  _10,
  input  _11,
  input  _12,
  input  _13,
  input  _14,
  input  _15,
  output [3:0] out_17,
  output Error
);

  wire xnor_1_out;
  wire [3:0] or_1_out;

  NotExactlyOne xnor_1 (
    .out(xnor_1_out), .in0(_0), .in1(_1), .in2(_2), .in3(_3), .in4(_4), .in5(_5), .in6(_6), .in7(_7),
    .in8(_8), .in9(_9), .in10(_10), .in11(_11), .in12(_12), .in13(_13), .in14(_14), .in15(_15));
  Transistor #(.\type ("n"), .gate("br")) transistor_1 (.in(xnor_1_out), .out(Error), .gate(xnor_1_out));
  Transistor transistor_2 (.in(_0), .out(Error), .gate(xnor_1_out));
  or or_1 (or_1_out[0], _9, _1, _11, _3, _5, _13, _7, _15);
  or or_2 (or_1_out[1], _10, _2, _11, _3, _6, _14, _7, _15);
  or or_3 (or_1_out[2], _12, _4, _13, _5, _6, _14, _7, _15);
  or or_4 (or_1_out[3], _12, _8, _13, _9, _10, _14, _11, _15);
  Transistor #(.gate("br"), .width(4)) transistor_3 (.in(or_1_out), .out(out_17), .gate(Error));
  Transistor #(.\type ("n"), .width(4)) transistor_4 (.in(4'b0000), .out(out_17), .gate(Error));
endmodule

module deencoder (
  input  [3:0] in_1
);

  wire _0000_out, _0001_out, _0010_out, _0011_out, _0100_out, _0101_out, _0110_out, _0111_out, _1000_out,
       _1001_out, _1010_out, _1011_out, _1100_out, _1101_out, _1110_out, _1111_out, A_out, B_out, C_out,
       D_out, E_out, F_out, G_out, not_1_out, not_2_out, not_3_out, not_4_out, not_5_out, not_6_out,
       not_7_out, not_8_out, not_9_out, not_10_out, not_11_out, not_12_out, not_13_out, not_14_out,
       not_15_out, not_16_out, not_17_out, not_18_out, not_19_out, not_20_out, not_21_out, not_22_out,
       not_23_out, not_24_out, not_25_out, not_26_out, not_27_out, not_28_out, not_29_out, not_30_out,
       not_31_out, not_32_out;

  not not_1 (not_1_out, in_1[3]);
  not not_2 (not_2_out, in_1[2]);
  not not_3 (not_3_out, in_1[1]);
  not not_4 (not_4_out, in_1[0]);
  not not_5 (not_5_out, in_1[3]);
  not not_6 (not_6_out, in_1[2]);
  not not_7 (not_7_out, in_1[1]);
  not not_8 (not_8_out, in_1[3]);
  not not_9 (not_9_out, in_1[2]);
  not not_10 (not_10_out, in_1[0]);
  not not_11 (not_11_out, in_1[3]);
  not not_12 (not_12_out, in_1[2]);
  not not_13 (not_13_out, in_1[3]);
  not not_14 (not_14_out, in_1[1]);
  not not_15 (not_15_out, in_1[0]);
  not not_16 (not_16_out, in_1[3]);
  not not_17 (not_17_out, in_1[1]);
  not not_18 (not_18_out, in_1[3]);
  not not_19 (not_19_out, in_1[0]);
  not not_20 (not_20_out, in_1[3]);
  not not_21 (not_21_out, in_1[2]);
  not not_22 (not_22_out, in_1[1]);
  not not_23 (not_23_out, in_1[0]);
  not not_24 (not_24_out, in_1[2]);
  not not_25 (not_25_out, in_1[1]);
  not not_26 (not_26_out, in_1[2]);
  not not_27 (not_27_out, in_1[0]);
  not not_28 (not_28_out, in_1[2]);
  not not_29 (not_29_out, in_1[1]);
  not not_30 (not_30_out, in_1[0]);
  not not_31 (not_31_out, in_1[1]);
  not not_32 (not_32_out, in_1[0]);
  and _0000 (_0000_out, not_1_out, not_2_out, not_3_out, not_4_out);
  and _0001 (_0001_out, not_5_out, not_6_out, not_7_out, in_1[0]);
  and _0010 (_0010_out, not_8_out, not_9_out, in_1[1], not_10_out);
  and _0011 (_0011_out, not_11_out, not_12_out, in_1[1], in_1[0]);
  and _0100 (_0100_out, not_13_out, in_1[2], not_14_out, not_15_out);
  and _0101 (_0101_out, not_16_out, in_1[2], not_17_out, in_1[0]);
  and _0110 (_0110_out, not_18_out, in_1[2], in_1[1], not_19_out);
  and _0111 (_0111_out, not_20_out, in_1[2], in_1[1], in_1[0]);
  and _1000 (_1000_out, in_1[3], not_21_out, not_22_out, not_23_out);
  and _1001 (_1001_out, in_1[3], not_24_out, not_25_out, in_1[0]);
  and _1010 (_1010_out, in_1[3], not_26_out, in_1[1], not_27_out);
  and _1011 (_1011_out, in_1[3], not_28_out, in_1[1], in_1[0]);
  and _1100 (_1100_out, in_1[3], in_1[2], not_29_out, not_30_out);
  and _1101 (_1101_out, in_1[3], in_1[2], not_31_out, in_1[0]);
  and _1110 (_1110_out, in_1[3], in_1[2], in_1[1], not_32_out);
  and _1111 (_1111_out, in_1[3], in_1[2], in_1[1], in_1[0]);
  or B (B_out, _0000_out, _0001_out, _0010_out, _0011_out, _0100_out, _0111_out, _1000_out, _1001_out, _1010_out, _1101_out);
  or A (A_out, _0000_out, _0010_out, _0110_out, _0101_out, _0011_out, _0111_out, _1000_out, _1001_out, _1010_out, _1111_out, _1100_out, _1110_out);
  or F (F_out, _0000_out, _0100_out, _0101_out, _1000_out, _1001_out, _1010_out, _1011_out, _0110_out, _1100_out, _1110_out, _1111_out);
  or G (G_out, _0010_out, _0011_out, _0100_out, _0101_out, _0110_out, _1000_out, _1001_out, _1010_out, _1011_out, _1101_out, _1110_out, _1111_out);
  or E (E_out, _0000_out, _0010_out, _0110_out, _1000_out, _1010_out, _1100_out, _1101_out, _1110_out, _1111_out, _1011_out);
  or D (D_out, _0000_out, _0010_out, _0011_out, _0101_out, _0110_out, _1000_out, _1001_out, _1011_out, _1100_out, _1101_out, _1110_out);
  or C (C_out, _0000_out, _0001_out, _0011_out, _0100_out, _0101_out, _0110_out, _0111_out, _1000_out, _1001_out, _1010_out, _1011_out, _1101_out);
  _7_Segment_Display u_7_segment_display_1 (
    .g(G_out), .f(F_out), .a(A_out), .b(B_out), .e(E_out), .d(D_out), .c(C_out));  // open: dp

  // Other names for the same wires on the sheet: _0 = in_1[0]; _1 = in_1[1]; _2 = in_1[2]; _3 = in_1[3]
endmodule

module multiplexor (
  input  [2:0] in_1,
  input  in_2,
  input  in_3,
  input  in_4,
  input  in_5,
  input  in_6,
  input  in_7,
  input  in_8,
  input  in_9,
  output out_10
);

  wire and_1_out, and_2_out, and_3_out, and_4_out, and_5_out, and_6_out, and_7_out, and_8_out, not_1_out,
       not_2_out, not_3_out, not_4_out, not_5_out, not_6_out, not_7_out, not_8_out, not_9_out, not_10_out,
       not_11_out, not_12_out;

  not not_1 (not_1_out, in_1[0]);
  not not_2 (not_2_out, in_1[1]);
  not not_3 (not_3_out, in_1[2]);
  not not_4 (not_4_out, in_1[1]);
  not not_5 (not_5_out, in_1[2]);
  not not_6 (not_6_out, in_1[0]);
  not not_7 (not_7_out, in_1[2]);
  not not_8 (not_8_out, in_1[2]);
  not not_9 (not_9_out, in_1[0]);
  not not_10 (not_10_out, in_1[1]);
  not not_11 (not_11_out, in_1[1]);
  not not_12 (not_12_out, in_1[0]);
  and and_1 (and_1_out, not_1_out, not_2_out, not_3_out, in_2);
  and and_2 (and_2_out, in_1[0], not_4_out, not_5_out, in_3);
  and and_3 (and_3_out, not_6_out, in_1[1], not_7_out, in_4);
  and and_4 (and_4_out, in_1[0], in_1[1], not_8_out, in_5);
  and and_5 (and_5_out, not_9_out, not_10_out, in_1[2], in_6);
  and and_6 (and_6_out, in_1[0], not_11_out, in_1[2], in_7);
  and and_7 (and_7_out, not_12_out, in_1[1], in_1[2], in_8);
  and and_8 (and_8_out, in_1[0], in_1[1], in_1[2], in_9);
  or or_1 (out_10, and_1_out, and_2_out, and_3_out, and_4_out, and_5_out, and_6_out, and_7_out, and_8_out);
endmodule

module demultiplexor (
  input  in_1,
  input  [2:0] in_2,
  output out_3,
  output out_4,
  output out_5,
  output out_6,
  output out_7,
  output out_8,
  output out_9,
  output out_10
);

  wire not_1_out, not_2_out, not_3_out, not_4_out, not_5_out, not_6_out, not_7_out, not_8_out, not_9_out,
       not_10_out, not_11_out, not_12_out;

  not not_1 (not_1_out, in_2[0]);
  not not_2 (not_2_out, in_2[1]);
  not not_3 (not_3_out, in_2[2]);
  not not_4 (not_4_out, in_2[1]);
  not not_5 (not_5_out, in_2[2]);
  not not_6 (not_6_out, in_2[0]);
  not not_7 (not_7_out, in_2[2]);
  not not_8 (not_8_out, in_2[2]);
  not not_9 (not_9_out, in_2[0]);
  not not_10 (not_10_out, in_2[1]);
  not not_11 (not_11_out, in_2[1]);
  not not_12 (not_12_out, in_2[0]);
  and and_1 (out_3, not_1_out, not_2_out, not_3_out, in_1);
  and and_2 (out_4, in_2[0], not_4_out, not_5_out, in_1);
  and and_3 (out_5, not_6_out, in_2[1], not_7_out, in_1);
  and and_4 (out_6, in_2[0], in_2[1], not_8_out, in_1);
  and and_5 (out_7, not_9_out, not_10_out, in_2[2], in_1);
  and and_6 (out_8, in_2[0], not_11_out, in_2[2], in_1);
  and and_7 (out_9, not_12_out, in_2[1], in_2[2], in_1);
  and and_8 (out_10, in_2[0], in_2[1], in_2[2]);
endmodule

module ALU (
  input  in_1,
  input  [2:0] in_2,
  input  [7:0] A,
  input  [7:0] B,
  input  [2:0] SEL,
  output out_6,
  output out_7,
  output [7:0] out_8
);

  wire [7:0] and_1_out, multiplexer_2_out, or_1_out, ripple_carry_adder_1_s, shifter_1_out, shifter_2_out,
       shifter_3_out, subtractor_1_out_5, xor_1_out;

  // Probe on A
  // Probe on B
  // Probe on ripple_carry_adder_1_s
  Ripple_Carry_Adder ripple_carry_adder_1 (.A(A), .B(B), .Cout(out_6), .S(ripple_carry_adder_1_s), .in_1(1'b0));
  // Probe on subtractor_1_out_5
  Subtractor subtractor_1 (.in_1(A), .in_2(B), .out_4(out_7), .out_5(subtractor_1_out_5), .in_3(1'b1));
  assign and_1_out = A & B;  // AND_Gate and_1, 8 bits wide
  // Probe on and_1_out
  Multiplexer #(.select(3), .width(8)) multiplexer_1 (
    .in0(ripple_carry_adder_1_s), .in1(subtractor_1_out_5), .in2(and_1_out), .in3(or_1_out), .in4(xor_1_out),
    .in5(shifter_3_out), .in6(shifter_2_out), .in7(shifter_1_out), .out(out_8), .sel(SEL), .en(1'b1));
  assign or_1_out = A | B;  // OR_Gate or_1, 8 bits wide
  // Probe on or_1_out
  assign xor_1_out = A ^ B;  // XOR_Gate xor_1, 8 bits wide
  // Probe on xor_1_out
  Multiplexer #(.width(8)) multiplexer_2 (.in0(A), .in1(B), .out(multiplexer_2_out), .sel(in_1), .en(1'b1));
  Shifter shifter_1 (.in(multiplexer_2_out), .\dist (in_2), .out(shifter_1_out));
  Shifter #(.shift("lr")) shifter_2 (.in(multiplexer_2_out), .\dist (in_2), .out(shifter_2_out));
  Shifter shifter_3 (.in(multiplexer_2_out), .\dist (in_2), .out(shifter_3_out));
  // Probe on shifter_1_out
  // Probe on shifter_2_out
  // Probe on shifter_3_out
endmodule
