// Logisim project 2lab.circ as structural Verilog: 3 circuits, main circuit YY
module CPU (
  input  [1:0] in_1,
  output out_2,
  output ZERO,
  output NEGATE
);

  wire clock_1_out, CLR_out, demultiplexer_1_out0, demultiplexer_1_out1, demultiplexer_1_out2,
       demultiplexer_1_out3, EN_CT, GOTO_DATA, LOAD_ADR, SAVE_DATA, SAVE_INS_ADR, SAVETO_REG;
  wire [3:0] ALU, bit_extender_1_out, INS;
  wire [7:0] ADR, counter_1_q, multiplexer_1_out;
  wire [15:0] adder_1_out, and_1_out, multiplexer_2_out, multiplexer_3_out, not_1_out, or_1_out, ram_1_data,
       register_1_q, register_2_q, register_3_q, register_4_q, shifter_1_out, shifter_2_out, shifter_3_out,
       subtractor_1_out, xor_1_out;

  // Probe on ALU
  Counter counter_1 (
    .load(LOAD_ADR), .D(ADR), .count(EN_CT), .Q(counter_1_q), .clk(clock_1_out), .clr(CLR_out));  // open: carry
  Clock clock_1 (.out(clock_1_out));
  // Probe on {ALU, INS}
  // Probe on INS
  // Probe on ALU
  Multiplexer #(.width(8)) multiplexer_1 (
    .in0(counter_1_q), .in1(ADR), .out(multiplexer_1_out), .sel(GOTO_DATA));  // open: en
  // Probe on INS[3:2]
  // Probe on ram_1_data
  RAM #(.dataWidth(16), .bus("separate")) ram_1 (
    .addr(multiplexer_1_out), .din(multiplexer_3_out), .data(ram_1_data), .str(SAVE_DATA), .clk(clock_1_out));  // open: sel, ld, clr
  // Probe on ram_1_data[7:0]
  YY yy_1 (
    .x0(INS[0]), .x1(INS[1]), .LOADadr(LOAD_ADR), .EnableCount(EN_CT), .Go2Data(GOTO_DATA),
    .SaveData(SAVE_DATA), .SaveInsData(SAVE_INS_ADR), .Save2Reg(SAVETO_REG), .in_3(clock_1_out),
    .in_4(CLR_out));
  // Probe on {ALU, INS}
  Register u_INS (.D(ram_1_data[15:8]), .en(SAVE_INS_ADR), .Q({ALU, INS}), .clk(clock_1_out), .clr(CLR_out));
  Register u_ADR (.D(ram_1_data[7:0]), .en(SAVE_INS_ADR), .Q(ADR), .clk(clock_1_out), .clr(CLR_out));
  Button CLR (.out(CLR_out));
  assign not_1_out = ~ram_1_data;  // NOT_Gate not_1, 16 bits wide
  Bit_Extender #(.in_width(16), .out_width(4)) bit_extender_1 (.in(ram_1_data), .out(bit_extender_1_out));
  assign and_1_out = ram_1_data & multiplexer_3_out;  // AND_Gate and_1, 16 bits wide
  assign or_1_out = ram_1_data | multiplexer_3_out;  // OR_Gate or_1, 16 bits wide
  assign xor_1_out = ram_1_data ^ multiplexer_3_out;  // XOR_Gate xor_1, 16 bits wide
  Adder #(.width(16)) adder_1 (.a(ram_1_data), .b(multiplexer_3_out), .out(adder_1_out), .cout(out_2));  // open: cin
  Subtractor #(.width(16)) subtractor_1 (
    .a(ram_1_data), .b(multiplexer_3_out), .out(subtractor_1_out));  // open: bin, bout
  Shifter #(.width(16)) shifter_1 (.in(ram_1_data), .\dist (bit_extender_1_out), .out(shifter_1_out));
  Shifter #(.width(16), .shift("lr")) shifter_2 (.\dist (bit_extender_1_out), .out(shifter_2_out));  // open: in
  Shifter #(.width(16), .shift("ar")) shifter_3 (.\dist (bit_extender_1_out), .out(shifter_3_out));  // open: in
  Demultiplexer #(.select(2)) demultiplexer_1 (
    .out0(demultiplexer_1_out0), .out1(demultiplexer_1_out1), .out2(demultiplexer_1_out2),
    .out3(demultiplexer_1_out3), .in(SAVETO_REG), .sel(INS[3:2]));  // open: en
  // Probe on multiplexer_2_out
  Multiplexer #(.select(4), .width(16)) multiplexer_2 (
    .in0(ram_1_data), .in1(not_1_out), .in2(and_1_out), .in3(or_1_out), .in4(xor_1_out), .in5(adder_1_out),
    .in6(subtractor_1_out), .in7(shifter_1_out), .in8(shifter_2_out), .in9(shifter_3_out),
    .out(multiplexer_2_out), .sel(ALU));  // open: in10, in11, in12, in13, in14, in15, en
  Register #(.width(16)) register_1 (
    .D(multiplexer_2_out), .en(demultiplexer_1_out0), .Q(register_1_q), .clk(clock_1_out), .clr(CLR_out));
  Register #(.width(16)) register_2 (
    .D(multiplexer_2_out), .en(demultiplexer_1_out1), .Q(register_2_q), .clk(clock_1_out), .clr(CLR_out));
  Register #(.width(16)) register_3 (
    .D(multiplexer_2_out), .en(demultiplexer_1_out2), .Q(register_3_q), .clk(clock_1_out), .clr(CLR_out));
  Register #(.width(16)) register_4 (
    .D(multiplexer_2_out), .en(demultiplexer_1_out3), .Q(register_4_q), .clk(clock_1_out), .clr(CLR_out));
  // Probe on multiplexer_3_out
  // Probe on multiplexer_3_out
  Multiplexer #(.select(2), .width(16)) multiplexer_3 (
    .in0(register_1_q), .in1(register_2_q), .in2(register_3_q), .in3(register_4_q), .out(multiplexer_3_out),
    .sel(INS[3:2]));  // open: en
  Comparator #(.width(16)) comparator_1 (.a(multiplexer_3_out), .b({16{1'b0}}), .eq(ZERO), .lt(NEGATE));  // open: gt

  // Other names for the same wires on the sheet: INS[7:4] = ALU; REG_ADR[1:0] = INS[3:2]
endmodule

module YY (
  input  x0,
  input  x1,
  input  in_3,
  input  in_4,
  output LOADadr,
  output EnableCount,
  output Go2Data,
  output SaveData,
  output SaveInsData,
  output Save2Reg
);

  wire and_1_out, and_2_out, and_3_out, and_4_out, not_1_out, not_2_out, not_3_out, not_4_out, not_5_out,
       not_6_out, not_7_out, not_8_out, not_9_out, not_10_out, not_11_out, not_12_out, not_13_out,
       not_14_out, not_15_out, or_1_out, xor_1_out, Z0_q, Z1_q;

  not not_1 (not_1_out, LOADadr);
  not not_2 (not_2_out, Z1_q);
  not not_3 (not_3_out, LOADadr);
  not not_4 (not_4_out, Z1_q);
  xor xor_1 (xor_1_out, x0, x1);
  not not_5 (not_5_out, LOADadr);
  not not_6 (not_6_out, Z1_q);
  not not_7 (not_7_out, Z0_q);
  not not_8 (not_8_out, LOADadr);
  not not_9 (not_9_out, Z1_q);
  not not_10 (not_10_out, x1);
  and and_1 (and_1_out, not_1_out, not_2_out, Z0_q, x0, x1);
  and and_2 (and_2_out, not_3_out, not_4_out, Z0_q, xor_1_out);
  and and_3 (and_3_out, not_5_out, not_6_out, not_7_out);
  and and_4 (and_4_out, not_8_out, not_9_out, Z0_q, x0, not_10_out);
  or or_1 (or_1_out, and_3_out, and_4_out);
  D_Flip_Flop Z2 (.clk(in_3), .D(and_1_out), .Q(LOADadr), .reset(in_4));  // open: Qn, preset, en
  D_Flip_Flop Z1 (.clk(in_3), .D(and_2_out), .Q(Z1_q), .reset(in_4));  // open: Qn, preset, en
  D_Flip_Flop Z0 (.clk(in_3), .D(or_1_out), .Q(Z0_q), .reset(in_4));  // open: Qn, preset, en
  not not_11 (not_11_out, Z1_q);
  or or_2 (Go2Data, Z1_q, LOADadr);
  and and_5 (SaveData, Z1_q, Z0_q);
  not not_12 (not_12_out, LOADadr);
  not not_13 (not_13_out, Z1_q);
  not not_14 (not_14_out, Z0_q);
  not not_15 (not_15_out, Z0_q);
  and and_6 (EnableCount, not_11_out, Z0_q);
  and and_7 (SaveInsData, not_12_out, not_13_out, not_14_out);
  and and_8 (Save2Reg, Z1_q, not_15_out);
endmodule

module skebob (
  input  Z2,
  input  Z1,
  input  Z0,
  output LOADadr,
  output EnableCount,
  output Go2Data,
  output SaveData,
  output SaveInsData,
  output Save2Reg
);

  wire not_1_out, not_2_out, not_3_out, not_4_out, not_5_out;

  not not_1 (not_1_out, Z1);
  or or_1 (Go2Data, Z1, Z2);
  and and_1 (SaveData, Z1, Z0);
  not not_2 (not_2_out, Z2);
  not not_3 (not_3_out, Z1);
  not not_4 (not_4_out, Z0);
  not not_5 (not_5_out, Z0);
  and and_2 (EnableCount, not_1_out, Z0);
  and and_3 (SaveInsData, not_2_out, not_3_out, not_4_out);
  and and_4 (Save2Reg, Z1, not_5_out);

  assign LOADadr = Z2;
endmodule
