// Logisim project цп — копия.circ as structural Verilog: 2 circuits, main circuit main
module main (
  output OVERFLOW,
  output ZERO,
  output NEGATIVE
);

  wire clock_1_out, clr_out, demultiplexer_1_out0, demultiplexer_1_out1, demultiplexer_1_out2,
       demultiplexer_1_out3, EnableCount, Go2Data, LoadAdr, Save2Reg, SaveData, SaveInsData;
  wire [3:0] ALU, bit_extender_1_out, INSTR;
  wire [7:0] ADR, counter_1_q, multiplexer_1_out, ram_1_data, ram_1_data_2;
  wire [15:0] adder_1_out, and_1_out, multiplexer_2_out, multiplexer_3_out, not_1_out, or_1_out,
       register_1_q, register_2_q, register_3_q, register_4_q, shifter_1_out, subtractor_1_out;

  // Probe on ADR
  Clock clock_1 (.out(clock_1_out));
  Button clr (.out(clr_out));
  // Probe on ALU
  Counter counter_1 (
    .load(LoadAdr), .D(ADR), .count(EnableCount), .Q(counter_1_q), .clk(clock_1_out), .clr(clr_out));  // open: carry
  Multiplexer #(.width(8)) multiplexer_1 (
    .in0(counter_1_q), .in1(ADR), .out(multiplexer_1_out), .sel(Go2Data));  // open: en
  // Probe on INSTR[3:2]
  RAM #(.dataWidth(16), .bus("separate")) ram_1 (
    .addr(multiplexer_1_out), .din(multiplexer_3_out), .data({ram_1_data_2, ram_1_data}), .str(SaveData),
    .clk(clock_1_out));  // open: sel, ld, clr
  Register INSTRUCTION (.D(ram_1_data_2), .en(SaveInsData), .Q({ALU, INSTR}), .clk(clock_1_out), .clr(clr_out));
  Register ADRESS (.D(ram_1_data), .en(SaveInsData), .Q(ADR), .clk(clock_1_out), .clr(clr_out));
  \УУ  \u_уу_1  (
    .x0(INSTR[0]), .x1(INSTR[1]), .Clock(clock_1_out), .LoadAdr(LoadAdr), .EnableCount(EnableCount),
    .Go2Data(Go2Data), .SaveData(SaveData), .SaveInsAdr(SaveInsData), .Save2Reg(Save2Reg), .clr(clr_out));
  Bit_Extender #(.in_width(16), .out_width(4)) bit_extender_1 (.in(multiplexer_3_out), .out(bit_extender_1_out));
  assign not_1_out = ~{ram_1_data_2, ram_1_data};  // NOT_Gate not_1, 16 bits wide
  Adder #(.width(16)) adder_1 (
    .a({ram_1_data_2, ram_1_data}), .b(multiplexer_3_out), .out(adder_1_out));  // open: cin, cout
  Subtractor #(.width(16)) subtractor_1 (
    .a({ram_1_data_2, ram_1_data}), .b(multiplexer_3_out), .out(subtractor_1_out), .bout(OVERFLOW));  // open: bin
  assign and_1_out = {ram_1_data_2, ram_1_data} & multiplexer_3_out;  // AND_Gate and_1, 16 bits wide
  assign or_1_out = {ram_1_data_2, ram_1_data} | multiplexer_3_out;  // OR_Gate or_1, 16 bits wide
  Shifter #(.width(16)) shifter_1 (.in({ram_1_data_2, ram_1_data}), .\dist (bit_extender_1_out), .out(shifter_1_out));
  Multiplexer #(.select(4), .width(16)) multiplexer_2 (
    .in0({ram_1_data_2, ram_1_data}), .in1(not_1_out), .in2(adder_1_out), .in3(subtractor_1_out),
    .in4(and_1_out), .in5(or_1_out), .in6(shifter_1_out), .out(multiplexer_2_out), .sel(ALU));  // open: in7, in8, in9, in10, in11, in12, in13, in14, in15, en
  // Probe on multiplexer_2_out
  Demultiplexer #(.select(2)) demultiplexer_1 (
    .out0(demultiplexer_1_out0), .out1(demultiplexer_1_out1), .out2(demultiplexer_1_out2),
    .out3(demultiplexer_1_out3), .in(Save2Reg), .sel(INSTR[3:2]));  // open: en
  Register #(.width(16)) register_1 (
    .D(multiplexer_2_out), .en(demultiplexer_1_out0), .Q(register_1_q), .clk(clock_1_out), .clr(clr_out));
  Register #(.width(16)) register_2 (
    .D(multiplexer_2_out), .en(demultiplexer_1_out1), .Q(register_2_q), .clk(clock_1_out), .clr(clr_out));
  Register #(.width(16)) register_3 (
    .D(multiplexer_2_out), .en(demultiplexer_1_out2), .Q(register_3_q), .clk(clock_1_out), .clr(clr_out));
  Register #(.width(16)) register_4 (
    .D(multiplexer_2_out), .en(demultiplexer_1_out3), .Q(register_4_q), .clk(clock_1_out), .clr(clr_out));
  Multiplexer #(.select(2), .width(16)) multiplexer_3 (
    .in0(register_1_q), .in1(register_2_q), .in2(register_3_q), .in3(register_4_q), .out(multiplexer_3_out),
    .sel(INSTR[3:2]));  // open: en
  Comparator #(.width(16)) comparator_1 (.a(multiplexer_3_out), .b({16{1'b0}}), .eq(ZERO), .lt(NEGATIVE));  // open: gt

  // Other names for the same wires on the sheet: INSTR[7:4] = ALU; RegAdr[1:0] = INSTR[3:2]
endmodule

module \УУ  (
  input  clr,
  input  x0,
  input  x1,
  input  Clock,
  output LoadAdr,
  output EnableCount,
  output Go2Data,
  output SaveData,
  output SaveInsAdr,
  output Save2Reg
);

  wire jmp_out, nop_out, not_1_out, not_2_out, not_3_out, not_4_out, not_5_out, not_6_out, not_7_out,
       not_8_out, not_9_out, not_10_out, not_11_out, not_12_out, not_13_out, not_14_out, not_15_out,
       not_16_out, not_17_out, not_18_out, not_19_out, not_20_out, not_21_out, not_22_out, not_23_out,
       not_24_out, not_25_out, not_26_out, not_27_out, or_1_out, or_2_out, sav_2_out, sav_out, wrt_2_out,
       wrt_out, z0_q, z1_q, z2_q;

  not not_1 (not_1_out, z2_q);
  not not_2 (not_2_out, z1_q);
  not not_3 (not_3_out, z0_q);
  not not_4 (not_4_out, x1);
  not not_5 (not_5_out, z1_q);
  not not_6 (not_6_out, z0_q);
  not not_7 (not_7_out, x1);
  not not_8 (not_8_out, z2_q);
  not not_9 (not_9_out, z1_q);
  not not_10 (not_10_out, z0_q);
  not not_11 (not_11_out, x0);
  not not_12 (not_12_out, z2_q);
  not not_13 (not_13_out, z1_q);
  not not_14 (not_14_out, x0);
  not not_15 (not_15_out, z2_q);
  not not_16 (not_16_out, z1_q);
  not not_17 (not_17_out, z0_q);
  nor nop (nop_out, z2_q, z1_q, z0_q, x0, x1);
  and wrt (wrt_out, not_1_out, not_2_out, not_3_out, x0, not_4_out);
  and wrt_2 (wrt_2_out, z2_q, not_5_out, not_6_out, x0, not_7_out);
  and sav (sav_out, not_8_out, not_9_out, not_10_out, not_11_out, x1);
  and sav_2 (sav_2_out, not_12_out, not_13_out, z0_q, not_14_out, x1);
  and jmp (jmp_out, not_15_out, not_16_out, not_17_out, x0, x1);
  or or_1 (or_1_out, nop_out, wrt_2_out, jmp_out, sav_2_out);
  or or_2 (or_2_out, wrt_out, jmp_out);
  D_Flip_Flop #(.trigger("falling")) z0 (.clk(Clock), .D(sav_out), .Q(z0_q), .reset(clr));  // open: Qn, preset, en
  D_Flip_Flop #(.trigger("falling")) z1 (.clk(Clock), .D(or_1_out), .Q(z1_q), .reset(clr));  // open: Qn, preset, en
  D_Flip_Flop #(.trigger("falling")) z2 (.clk(Clock), .D(or_2_out), .Q(z2_q), .reset(clr));  // open: Qn, preset, en
  not not_18 (not_18_out, z0_q);
  not not_19 (not_19_out, z1_q);
  not not_20 (not_20_out, z2_q);
  not not_21 (not_21_out, z0_q);
  not not_22 (not_22_out, z1_q);
  not not_23 (not_23_out, z0_q);
  not not_24 (not_24_out, z2_q);
  not not_25 (not_25_out, z0_q);
  not not_26 (not_26_out, z1_q);
  not not_27 (not_27_out, z2_q);
  and and_1 (SaveInsAdr, not_18_out, not_19_out, not_20_out);
  and and_2 (Save2Reg, not_21_out, not_22_out, z2_q);
  and and_3 (EnableCount, not_23_out, z1_q, not_24_out);
  and and_4 (LoadAdr, not_25_out, z1_q, z2_q);
  and and_5 (SaveData, z0_q, not_26_out, not_27_out);
  or or_3 (Go2Data, Save2Reg, SaveData);
endmodule
