// Logisim project 5lab1.circ as structural Verilog: 5 circuits, main circuit main
module main (
  input  CLR
);

  wire clock_1_out, d_ff_1_q, dictionary_1_and, dictionary_1_jmp, dictionary_1_nop, dictionary_1_or,
       n1ap_1_done, n2ap_1_out_5, or_1_out, transistor_1_out;
  wire [3:0] counter_1_q;
  wire [6:0] keyboard_1_data;
  wire [7:0] controlled_buffer_1_out, n1ap_1_res, n2ap_1_out_6;

  Keyboard keyboard_1 (.clk(clock_1_out), .clr(CLR), .data(keyboard_1_data));  // open: re, avail
  Clock clock_1 (.out(clock_1_out));
  TTY tty_1 (.data(keyboard_1_data), .clk(clock_1_out), .clr(CLR));  // open: we
  // Probe on keyboard_1_data
  // Probe on keyboard_1_data
  dictionary dictionary_1 (
    .JMP(dictionary_1_jmp), .AND(dictionary_1_and), .OR(dictionary_1_or), .NOP(dictionary_1_nop),
    .in_1(clock_1_out), .in_2(keyboard_1_data));
  _1ap u_1ap_1 (
    .CLK(clock_1_out), .JMP(dictionary_1_jmp), .DONE(n1ap_1_done), .RES(n1ap_1_res), .in_3(keyboard_1_data));
  assign controlled_buffer_1_out = n1ap_1_done ? n1ap_1_res : 8'bz;  // Controlled_Buffer controlled_buffer_1
  _2ap u_2ap_1 (
    .in_1(clock_1_out), .out_5(n2ap_1_out_5), .in_2(keyboard_1_data), .AND(dictionary_1_and),
    .OR(dictionary_1_or), .out_6(n2ap_1_out_6));
  assign controlled_buffer_1_out = n2ap_1_out_5 ? n2ap_1_out_6 : 8'bz;  // Controlled_Buffer controlled_buffer_2
  assign controlled_buffer_1_out = dictionary_1_nop ? {8{1'b0}} : 8'bz;  // Controlled_Buffer controlled_buffer_3
  Counter #(.width(4), .max('hf)) counter_1 (
    .Q(counter_1_q), .clk(transistor_1_out), .clr(CLR));  // open: load, D, count, carry
  Transistor #(.gate("br")) transistor_1 (.in(1'b0), .out(transistor_1_out), .gate(d_ff_1_q));
  or or_1 (or_1_out, n1ap_1_done, n2ap_1_out_5, dictionary_1_nop);
  Transistor #(.\type ("n"), .gate("br")) transistor_2 (.in(1'b1), .out(transistor_1_out), .gate(d_ff_1_q));
  D_Flip_Flop d_ff_1 (.clk(clock_1_out), .D(or_1_out), .Q(d_ff_1_q));  // open: Qn, preset, en, reset
  RAM #(.addrWidth(4), .bus("separate")) ram_1 (
    .addr(counter_1_q), .din(controlled_buffer_1_out), .clk(transistor_1_out), .clr(CLR));  // open: data, str, sel, ld

  // Notes on the sheet:
  //   cmd reg adr
endmodule

module dictionary (
  input  in_1,
  input  [6:0] in_2,
  output JMP,
  output AND,
  output OR,
  output NOP
);

  wire and_1_out, and_2_out, and_3_out, and_4_out, and_5_out, and_6_out, and_7_out, and_8_out, and_9_out,
       and_10_out, comparator_1_eq, comparator_2_eq, comparator_3_eq, comparator_4_eq, comparator_5_eq,
       comparator_6_eq, comparator_7_eq, comparator_8_eq, comparator_9_eq, comparator_10_eq,
       comparator_11_eq, comparator_12_eq, comparator_13_eq, comparator_14_eq, d_ff_1_q, d_ff_2_q, d_ff_3_q,
       d_ff_5_q, d_ff_6_q, d_ff_8_q, d_ff_9_q, d_ff_10_q, d_ff_12_q, d_ff_13_q;

  Comparator #(.width(7)) comparator_1 (.a(in_2), .b(7'b1001010), .eq(comparator_1_eq));  // open: gt, lt
  Comparator #(.width(7)) comparator_2 (.a(in_2), .b(7'b1001101), .eq(comparator_2_eq));  // open: gt, lt
  Comparator #(.width(7)) comparator_3 (.a(in_2), .b(7'b1010000), .eq(comparator_3_eq));  // open: gt, lt
  Comparator #(.width(7)) comparator_4 (.a(in_2), .b(7'b0100000), .eq(comparator_4_eq));  // open: gt, lt
  Comparator #(.width(7)) comparator_5 (.a(in_2), .b(7'b1001111), .eq(comparator_5_eq));  // open: gt, lt
  Comparator #(.width(7)) comparator_6 (.a(in_2), .b(7'b1010010), .eq(comparator_6_eq));  // open: gt, lt
  Comparator #(.width(7)) comparator_7 (.a(in_2), .b(7'b0100000), .eq(comparator_7_eq));  // open: gt, lt
  D_Flip_Flop d_ff_1 (.clk(in_1), .D(comparator_1_eq), .Q(d_ff_1_q));  // open: Qn, preset, en, reset
  D_Flip_Flop d_ff_2 (.clk(in_1), .D(and_1_out), .Q(d_ff_2_q));  // open: Qn, preset, en, reset
  and and_1 (and_1_out, d_ff_1_q, comparator_2_eq);
  D_Flip_Flop d_ff_3 (.clk(in_1), .D(and_2_out), .Q(d_ff_3_q));  // open: Qn, preset, en, reset
  and and_2 (and_2_out, d_ff_2_q, comparator_3_eq);
  D_Flip_Flop d_ff_4 (.clk(in_1), .D(and_3_out), .Q(JMP));  // open: Qn, preset, en, reset
  and and_3 (and_3_out, d_ff_3_q, comparator_4_eq);
  D_Flip_Flop d_ff_5 (.clk(in_1), .D(comparator_5_eq), .Q(d_ff_5_q));  // open: Qn, preset, en, reset
  D_Flip_Flop d_ff_6 (.clk(in_1), .D(and_4_out), .Q(d_ff_6_q));  // open: Qn, preset, en, reset
  and and_4 (and_4_out, d_ff_5_q, comparator_6_eq);
  D_Flip_Flop d_ff_7 (.clk(in_1), .D(and_5_out), .Q(OR));  // open: Qn, preset, en, reset
  and and_5 (and_5_out, d_ff_6_q, comparator_7_eq);
  // Probe on in_2
  Comparator #(.width(7)) comparator_8 (.a(in_2), .b(7'b1000001), .eq(comparator_8_eq));  // open: gt, lt
  and and_6 (and_6_out, d_ff_8_q, comparator_9_eq);
  Comparator #(.width(7)) comparator_9 (.a(in_2), .b(7'b1001110), .eq(comparator_9_eq));  // open: gt, lt
  and and_7 (and_7_out, d_ff_9_q, comparator_10_eq);
  Comparator #(.width(7)) comparator_10 (.a(in_2), .b(7'b1000100), .eq(comparator_10_eq));  // open: gt, lt
  and and_8 (and_8_out, d_ff_10_q, comparator_11_eq);
  Comparator #(.width(7)) comparator_11 (.a(in_2), .b(7'b0100000), .eq(comparator_11_eq));  // open: gt, lt
  Comparator #(.width(7)) comparator_12 (.a(in_2), .b(7'b1001110), .eq(comparator_12_eq));  // open: gt, lt
  and and_9 (and_9_out, d_ff_12_q, comparator_13_eq);
  Comparator #(.width(7)) comparator_13 (.a(in_2), .b(7'b1001111), .eq(comparator_13_eq));  // open: gt, lt
  and and_10 (and_10_out, d_ff_13_q, comparator_14_eq);
  Comparator #(.width(7)) comparator_14 (.a(in_2), .b(7'b1010000), .eq(comparator_14_eq));  // open: gt, lt
  D_Flip_Flop d_ff_8 (.clk(in_1), .D(comparator_8_eq), .Q(d_ff_8_q));  // open: Qn, preset, en, reset
  D_Flip_Flop d_ff_9 (.clk(in_1), .D(and_6_out), .Q(d_ff_9_q));  // open: Qn, preset, en, reset
  D_Flip_Flop d_ff_10 (.clk(in_1), .D(and_7_out), .Q(d_ff_10_q));  // open: Qn, preset, en, reset
  D_Flip_Flop d_ff_11 (.clk(in_1), .D(and_8_out), .Q(AND));  // open: Qn, preset, en, reset
  D_Flip_Flop d_ff_12 (.clk(in_1), .D(comparator_12_eq), .Q(d_ff_12_q));  // open: Qn, preset, en, reset
  D_Flip_Flop d_ff_13 (.clk(in_1), .D(and_9_out), .Q(d_ff_13_q));  // open: Qn, preset, en, reset
  D_Flip_Flop d_ff_14 (.clk(in_1), .D(and_10_out), .Q(NOP));  // open: Qn, preset, en, reset
endmodule

module decryptor (
  input  [6:0] in_1,
  output [1:0] _2D,
  output [3:0] _4D
);

  wire comparator_1_eq, comparator_2_eq, comparator_3_eq, comparator_4_eq, comparator_5_eq, comparator_6_eq,
       comparator_7_eq, comparator_8_eq, comparator_9_eq, comparator_10_eq, comparator_11_eq,
       comparator_12_eq, comparator_13_eq, comparator_14_eq, comparator_15_eq, comparator_16_eq;

  Comparator #(.width(7)) comparator_1 (.a(in_1), .b(7'b0110000), .eq(comparator_1_eq));  // open: gt, lt
  Comparator #(.width(7)) comparator_2 (.a(in_1), .b(7'b0110001), .eq(comparator_2_eq));  // open: gt, lt
  Comparator #(.width(7)) comparator_3 (.a(in_1), .b(7'b0110010), .eq(comparator_3_eq));  // open: gt, lt
  Comparator #(.width(7)) comparator_4 (.a(in_1), .b(7'b0110011), .eq(comparator_4_eq));  // open: gt, lt
  Comparator #(.width(7)) comparator_5 (.a(in_1), .b(7'b0110100), .eq(comparator_5_eq));  // open: gt, lt
  Comparator #(.width(7)) comparator_6 (.a(in_1), .b(7'b0110101), .eq(comparator_6_eq));  // open: gt, lt
  Comparator #(.width(7)) comparator_7 (.a(in_1), .b(7'b0110110), .eq(comparator_7_eq));  // open: gt, lt
  Comparator #(.width(7)) comparator_8 (.a(in_1), .b(7'b0110111), .eq(comparator_8_eq));  // open: gt, lt
  Comparator #(.width(7)) comparator_9 (.a(in_1), .b(7'b0111000), .eq(comparator_9_eq));  // open: gt, lt
  Comparator #(.width(7)) comparator_10 (.a(in_1), .b(7'b0111001), .eq(comparator_10_eq));  // open: gt, lt
  Comparator #(.width(7)) comparator_11 (.a(in_1), .b(7'b1000001), .eq(comparator_11_eq));  // open: gt, lt
  Comparator #(.width(7)) comparator_12 (.a(in_1), .b(7'b1000010), .eq(comparator_12_eq));  // open: gt, lt
  Comparator #(.width(7)) comparator_13 (.a(in_1), .b(7'b1000011), .eq(comparator_13_eq));  // open: gt, lt
  Comparator #(.width(7)) comparator_14 (.a(in_1), .b(7'b1000100), .eq(comparator_14_eq));  // open: gt, lt
  Comparator #(.width(7)) comparator_15 (.a(in_1), .b(7'b1000101), .eq(comparator_15_eq));  // open: gt, lt
  Comparator #(.width(7)) comparator_16 (.a(in_1), .b(7'b1000110), .eq(comparator_16_eq));  // open: gt, lt
  assign _4D = comparator_1_eq ? 4'b0000 : 4'bz;  // Controlled_Buffer controlled_buffer_1
  assign _4D = comparator_2_eq ? 4'b0001 : 4'bz;  // Controlled_Buffer controlled_buffer_2
  assign _4D = comparator_3_eq ? 4'b0010 : 4'bz;  // Controlled_Buffer controlled_buffer_3
  assign _4D = comparator_4_eq ? 4'b0011 : 4'bz;  // Controlled_Buffer controlled_buffer_4
  assign _4D = comparator_5_eq ? 4'b0100 : 4'bz;  // Controlled_Buffer controlled_buffer_5
  assign _4D = comparator_6_eq ? 4'b0101 : 4'bz;  // Controlled_Buffer controlled_buffer_6
  assign _4D = comparator_7_eq ? 4'b0110 : 4'bz;  // Controlled_Buffer controlled_buffer_7
  assign _4D = comparator_8_eq ? 4'b0111 : 4'bz;  // Controlled_Buffer controlled_buffer_8
  assign _4D = comparator_9_eq ? 4'b1000 : 4'bz;  // Controlled_Buffer controlled_buffer_9
  assign _4D = comparator_10_eq ? 4'b1001 : 4'bz;  // Controlled_Buffer controlled_buffer_10
  assign _4D = comparator_11_eq ? 4'b1010 : 4'bz;  // Controlled_Buffer controlled_buffer_11
  assign _4D = comparator_12_eq ? 4'b1011 : 4'bz;  // Controlled_Buffer controlled_buffer_12
  assign _4D = comparator_13_eq ? 4'b1100 : 4'bz;  // Controlled_Buffer controlled_buffer_13
  assign _4D = comparator_14_eq ? 4'b1101 : 4'bz;  // Controlled_Buffer controlled_buffer_14
  assign _4D = comparator_15_eq ? 4'b1110 : 4'bz;  // Controlled_Buffer controlled_buffer_15
  assign _4D = comparator_16_eq ? 4'b1111 : 4'bz;  // Controlled_Buffer controlled_buffer_16
  Bit_Extender #(.in_width(4), .out_width(2)) bit_extender_1 (.in(_4D), .out(_2D));
endmodule

module _1ap (
  input  CLK,
  input  JMP,
  input  [6:0] in_3,
  output DONE,
  output [7:0] RES
);

  wire [6:0] register_1_q;

  D_Flip_Flop d_ff_1 (.clk(CLK), .D(JMP), .Q(DONE));  // open: Qn, preset, en, reset
  Register #(.width(7)) register_1 (.D(in_3), .Q(register_1_q), .clk(DONE));  // open: en, clr
  decryptor decryptor_1 (._4D(RES[3:0]), .in_1(register_1_q));  // open: _2D

  assign RES[7:4] = 4'b0100;
endmodule

module _2ap (
  input  in_1,
  input  [6:0] in_2,
  input  AND,
  input  OR,
  output out_5,
  output [7:0] out_6
);

  wire d_ff_1_q, or_1_out, or_2_out;
  wire [1:0] controlled_buffer_1_out;
  wire [6:0] register_1_q, register_3_q;

  assign controlled_buffer_1_out = AND ? 2'b10 : 2'bz;  // Controlled_Buffer controlled_buffer_1
  or or_1 (or_1_out, AND, OR);
  or or_2 (or_2_out, OR, AND);
  assign controlled_buffer_1_out = OR ? 2'b11 : 2'bz;  // Controlled_Buffer controlled_buffer_2
  D_Flip_Flop d_ff_1 (.clk(in_1), .D(or_2_out), .Q(d_ff_1_q));  // open: Qn, preset, en, reset
  Register #(.width(7)) register_1 (.D(in_2), .Q(register_1_q), .clk(d_ff_1_q));  // open: en, clr
  decryptor decryptor_1 (._2D(out_6[5:4]), .in_1(register_1_q));  // open: _4D
  Register #(.width(2)) register_2 (.D(controlled_buffer_1_out), .Q(out_6[7:6]), .clk(or_1_out));  // open: en, clr
  D_Flip_Flop d_ff_2 (.clk(in_1), .D(d_ff_1_q), .Q(out_5));  // open: Qn, preset, en, reset
  Register #(.width(7)) register_3 (.D(in_2), .Q(register_3_q), .clk(out_5));  // open: en, clr
  decryptor decryptor_2 (._4D(out_6[3:0]), .in_1(register_3_q));  // open: _2D
endmodule
