// Logisim project Лаба25_Юрьев_Ярослав-2.circ as structural Verilog: 5 circuits, main circuit main
module main (
  input  CLR
);

  wire CLK, clock_1_out, d_ff_1_q, n1_append_1_done, n2_append_1_done, or_1_out, \словарь_1_and ,
       \словарь_1_jmp , \словарь_1_nop , \словарь_1_or ;
  wire [3:0] counter_1_q;
  wire [6:0] keyboard_1_data;
  wire [7:0] DATA, n1_append_1_res, n2_append_1_res, ram_1_data;

  Keyboard keyboard_1 (.clk(clock_1_out), .data(keyboard_1_data));  // open: re, clr, avail
  Clock clock_1 (.out(clock_1_out));
  // Probe on keyboard_1_data
  // Probe on keyboard_1_data
  TTY tty_1 (.data(keyboard_1_data), .clk(clock_1_out), .clr(CLR));  // open: we
  \словарь  \u_словарь_1  (
    .CLK(clock_1_out), .JMP(\словарь_1_jmp ), .AND(\словарь_1_and ), .OR(\словарь_1_or ),
    .NOP(\словарь_1_nop ), .IN(keyboard_1_data));
  assign DATA = \словарь_1_nop  ? {8{1'b0}} : 8'bz;  // Controlled_Buffer controlled_buffer_1
  _1_append u_1_append_1 (
    .CLK(clock_1_out), .JMP(\словарь_1_jmp ), .in_3(keyboard_1_data), .RES(n1_append_1_res),
    .DONE(n1_append_1_done));
  _2_APPEND u_2_append_1 (
    .CLK(clock_1_out), .in_2(keyboard_1_data), .AND(\словарь_1_and ), .OR(\словарь_1_or ),
    .DONE(n2_append_1_done), .RES(n2_append_1_res));
  assign DATA = n1_append_1_done ? n1_append_1_res : 8'bz;  // Controlled_Buffer controlled_buffer_2
  // Probe on DATA
  assign DATA = n2_append_1_done ? n2_append_1_res : 8'bz;  // Controlled_Buffer controlled_buffer_3
  Counter #(.width(4), .max('hf)) counter_1 (.Q(counter_1_q), .clk(CLK), .clr(CLR));  // open: load, D, count, carry
  Transistor #(.gate("br")) transistor_1 (.in(1'b0), .out(CLK), .gate(d_ff_1_q));
  or or_1 (or_1_out, n1_append_1_done, n2_append_1_done, \словарь_1_nop );
  Transistor #(.\type ("n"), .gate("br")) transistor_2 (.in(1'b1), .out(CLK), .gate(d_ff_1_q));
  RAM #(.addrWidth(4), .bus("separate")) ram_1 (
    .addr(counter_1_q), .din(DATA), .data(ram_1_data), .clk(CLK), .clr(CLR));  // open: str, sel, ld
  D_Flip_Flop d_ff_1 (.clk(clock_1_out), .D(or_1_out), .Q(d_ff_1_q));  // open: Qn, preset, en, reset

  // Notes on the sheet:
  //   ПРАВИЛА НАПИСАНИЯ:
  //   (CMD)(SPACE)(REG !для команд, где используется!)(ADR)
endmodule

module \словарь  (
  input  CLK,
  input  [6:0] IN,
  output JMP,
  output AND,
  output OR,
  output NOP
);

  wire and_1_out, and_2_out, and_3_out, and_4_out, and_5_out, and_6_out, and_7_out, and_8_out, and_9_out,
       and_10_out, comparator_1_eq, comparator_2_eq, comparator_3_eq, comparator_4_eq, comparator_5_eq,
       comparator_6_eq, comparator_7_eq, comparator_8_eq, comparator_9_eq, comparator_10_eq,
       comparator_11_eq, comparator_12_eq, comparator_13_eq, comparator_14_eq, d_ff_1_q, d_ff_2_q, d_ff_3_q,
       d_ff_4_q, d_ff_5_q, d_ff_6_q, d_ff_7_q, d_ff_8_q, d_ff_9_q, d_ff_10_q;

  // Probe on IN
  // Probe on IN
  D_Flip_Flop d_ff_1 (.clk(CLK), .D(comparator_1_eq), .Q(d_ff_1_q));  // open: Qn, preset, en, reset
  Comparator #(.width(7)) comparator_1 (.a(IN), .b(7'b1001010), .eq(comparator_1_eq));  // open: gt, lt
  and and_1 (and_1_out, d_ff_1_q, comparator_2_eq);
  Comparator #(.width(7)) comparator_2 (.a(IN), .b(7'b1001101), .eq(comparator_2_eq));  // open: gt, lt
  and and_2 (and_2_out, d_ff_5_q, comparator_3_eq);
  Comparator #(.width(7)) comparator_3 (.a(IN), .b(7'b1010000), .eq(comparator_3_eq));  // open: gt, lt
  and and_3 (and_3_out, d_ff_9_q, comparator_4_eq);
  Comparator #(.width(7)) comparator_4 (.a(IN), .b(7'b0100000), .eq(comparator_4_eq));  // open: gt, lt
  D_Flip_Flop d_ff_2 (.clk(CLK), .D(comparator_5_eq), .Q(d_ff_2_q));  // open: Qn, preset, en, reset
  Comparator #(.width(7)) comparator_5 (.a(IN), .b(7'b1000001), .eq(comparator_5_eq));  // open: gt, lt
  and and_4 (and_4_out, d_ff_2_q, comparator_6_eq);
  Comparator #(.width(7)) comparator_6 (.a(IN), .b(7'b1001110), .eq(comparator_6_eq));  // open: gt, lt
  and and_5 (and_5_out, d_ff_6_q, comparator_7_eq);
  Comparator #(.width(7)) comparator_7 (.a(IN), .b(7'b1000100), .eq(comparator_7_eq));  // open: gt, lt
  and and_6 (and_6_out, d_ff_10_q, comparator_8_eq);
  Comparator #(.width(7)) comparator_8 (.a(IN), .b(7'b0100000), .eq(comparator_8_eq));  // open: gt, lt
  D_Flip_Flop d_ff_3 (.clk(CLK), .D(comparator_9_eq), .Q(d_ff_3_q));  // open: Qn, preset, en, reset
  Comparator #(.width(7)) comparator_9 (.a(IN), .b(7'b1001111), .eq(comparator_9_eq));  // open: gt, lt
  and and_7 (and_7_out, d_ff_3_q, comparator_10_eq);
  Comparator #(.width(7)) comparator_10 (.a(IN), .b(7'b1010010), .eq(comparator_10_eq));  // open: gt, lt
  and and_8 (and_8_out, d_ff_7_q, comparator_11_eq);
  Comparator #(.width(7)) comparator_11 (.a(IN), .b(7'b0100000), .eq(comparator_11_eq));  // open: gt, lt
  D_Flip_Flop d_ff_4 (.clk(CLK), .D(comparator_12_eq), .Q(d_ff_4_q));  // open: Qn, preset, en, reset
  Comparator #(.width(7)) comparator_12 (.a(IN), .b(7'b1001110), .eq(comparator_12_eq));  // open: gt, lt
  and and_9 (and_9_out, d_ff_4_q, comparator_13_eq);
  Comparator #(.width(7)) comparator_13 (.a(IN), .b(7'b1001111), .eq(comparator_13_eq));  // open: gt, lt
  and and_10 (and_10_out, d_ff_8_q, comparator_14_eq);
  Comparator #(.width(7)) comparator_14 (.a(IN), .b(7'b1010000), .eq(comparator_14_eq));  // open: gt, lt
  D_Flip_Flop d_ff_5 (.clk(CLK), .D(and_1_out), .Q(d_ff_5_q));  // open: Qn, preset, en, reset
  D_Flip_Flop d_ff_6 (.clk(CLK), .D(and_4_out), .Q(d_ff_6_q));  // open: Qn, preset, en, reset
  D_Flip_Flop d_ff_7 (.clk(CLK), .D(and_7_out), .Q(d_ff_7_q));  // open: Qn, preset, en, reset
  D_Flip_Flop d_ff_8 (.clk(CLK), .D(and_9_out), .Q(d_ff_8_q));  // open: Qn, preset, en, reset
  D_Flip_Flop d_ff_9 (.clk(CLK), .D(and_2_out), .Q(d_ff_9_q));  // open: Qn, preset, en, reset
  D_Flip_Flop d_ff_10 (.clk(CLK), .D(and_5_out), .Q(d_ff_10_q));  // open: Qn, preset, en, reset
  D_Flip_Flop d_ff_11 (.clk(CLK), .D(and_8_out), .Q(OR));  // open: Qn, preset, en, reset
  D_Flip_Flop d_ff_12 (.clk(CLK), .D(and_10_out), .Q(NOP));  // open: Qn, preset, en, reset
  D_Flip_Flop d_ff_13 (.clk(CLK), .D(and_3_out), .Q(JMP));  // open: Qn, preset, en, reset
  D_Flip_Flop d_ff_14 (.clk(CLK), .D(and_6_out), .Q(AND));  // open: Qn, preset, en, reset
endmodule

module \дешифратор  (
  input  [6:0] in_1,
  output [3:0] _4_DIG,
  output [1:0] _2_DIG
);

  wire comparator_1_eq, comparator_2_eq, comparator_3_eq, comparator_4_eq, comparator_5_eq, comparator_6_eq,
       comparator_7_eq, comparator_8_eq, comparator_9_eq, comparator_10_eq, comparator_11_eq,
       comparator_12_eq, comparator_13_eq, comparator_14_eq, comparator_15_eq, comparator_16_eq;

  Comparator #(.width(7)) comparator_1 (.a(in_1), .b(7'b0110000), .eq(comparator_1_eq));  // open: gt, lt
  Comparator #(.width(7)) comparator_2 (.a(in_1), .b(7'b0110001), .eq(comparator_2_eq));  // open: gt, lt
  Comparator #(.width(7)) comparator_3 (.a(in_1), .b(7'b0110010), .eq(comparator_3_eq));  // open: gt, lt
  Comparator #(.width(7)) comparator_4 (.a(in_1), .b(7'b0110011), .eq(comparator_4_eq));  // open: gt, lt
  Comparator #(.width(7)) comparator_5 (.a(in_1), .b(7'b0110100), .eq(comparator_5_eq));  // open: gt, lt
  Comparator #(.width(7)) comparator_6 (.a(in_1), .b(7'b0110101), .eq(comparator_6_eq));  // open: gt, lt
  Comparator #(.width(7)) comparator_7 (.a(in_1), .b(7'b0110110), .eq(comparator_7_eq));  // open: gt, lt
  Comparator #(.width(7)) comparator_8 (.a(in_1), .b(7'b0110111), .eq(comparator_8_eq));  // open: gt, lt
  Comparator #(.width(7)) comparator_9 (.a(in_1), .b(7'b0111000), .eq(comparator_9_eq));  // open: gt, lt
  Comparator #(.width(7)) comparator_10 (.a(in_1), .b(7'b0111001), .eq(comparator_10_eq));  // open: gt, lt
  Comparator #(.width(7)) comparator_11 (.a(in_1), .b(7'b1000001), .eq(comparator_11_eq));  // open: gt, lt
  Comparator #(.width(7)) comparator_12 (.a(in_1), .b(7'b1000010), .eq(comparator_12_eq));  // open: gt, lt
  Comparator #(.width(7)) comparator_13 (.a(in_1), .b(7'b1000011), .eq(comparator_13_eq));  // open: gt, lt
  Comparator #(.width(7)) comparator_14 (.a(in_1), .b(7'b1000100), .eq(comparator_14_eq));  // open: gt, lt
  Comparator #(.width(7)) comparator_15 (.a(in_1), .b(7'b1000101), .eq(comparator_15_eq));  // open: gt, lt
  Comparator #(.width(7)) comparator_16 (.a(in_1), .b(7'b1000110), .eq(comparator_16_eq));  // open: gt, lt
  assign _4_DIG = comparator_1_eq ? 4'b0000 : 4'bz;  // Controlled_Buffer controlled_buffer_1
  assign _4_DIG = comparator_2_eq ? 4'b0001 : 4'bz;  // Controlled_Buffer controlled_buffer_2
  assign _4_DIG = comparator_3_eq ? 4'b0010 : 4'bz;  // Controlled_Buffer controlled_buffer_3
  assign _4_DIG = comparator_4_eq ? 4'b0011 : 4'bz;  // Controlled_Buffer controlled_buffer_4
  assign _4_DIG = comparator_5_eq ? 4'b0100 : 4'bz;  // Controlled_Buffer controlled_buffer_5
  assign _4_DIG = comparator_6_eq ? 4'b0101 : 4'bz;  // Controlled_Buffer controlled_buffer_6
  assign _4_DIG = comparator_7_eq ? 4'b0110 : 4'bz;  // Controlled_Buffer controlled_buffer_7
  assign _4_DIG = comparator_8_eq ? 4'b0111 : 4'bz;  // Controlled_Buffer controlled_buffer_8
  assign _4_DIG = comparator_9_eq ? 4'b1000 : 4'bz;  // Controlled_Buffer controlled_buffer_9
  assign _4_DIG = comparator_10_eq ? 4'b1001 : 4'bz;  // Controlled_Buffer controlled_buffer_10
  assign _4_DIG = comparator_11_eq ? 4'b1010 : 4'bz;  // Controlled_Buffer controlled_buffer_11
  assign _4_DIG = comparator_12_eq ? 4'b1011 : 4'bz;  // Controlled_Buffer controlled_buffer_12
  assign _4_DIG = comparator_13_eq ? 4'b1100 : 4'bz;  // Controlled_Buffer controlled_buffer_13
  assign _4_DIG = comparator_14_eq ? 4'b1101 : 4'bz;  // Controlled_Buffer controlled_buffer_14
  assign _4_DIG = comparator_15_eq ? 4'b1110 : 4'bz;  // Controlled_Buffer controlled_buffer_15
  assign _4_DIG = comparator_16_eq ? 4'b1111 : 4'bz;  // Controlled_Buffer controlled_buffer_16
  // Probe on _4_DIG
  Bit_Extender #(.in_width(4), .out_width(2)) bit_extender_1 (.in(_4_DIG), .out(_2_DIG));
endmodule

module _1_append (
  input  CLK,
  input  JMP,
  input  [6:0] in_3,
  output DONE,
  output [7:0] RES
);

  wire [6:0] register_1_q;

  D_Flip_Flop d_ff_1 (.clk(CLK), .D(JMP), .Q(DONE));  // open: Qn, preset, en, reset
  Register #(.width(7)) register_1 (.D(in_3), .Q(register_1_q), .clk(DONE));  // open: en, clr
  \дешифратор  \u_дешифратор_1  (.in_1(register_1_q), ._4_DIG(RES[3:0]));  // open: _2_DIG
  // Probe on RES[3:0]
  // Probe on {4'b0100, RES[3:0]}

  assign RES[7:4] = 4'b0100;
endmodule

module _2_APPEND (
  input  CLK,
  input  [6:0] in_2,
  input  AND,
  input  OR,
  output DONE,
  output [7:0] RES
);

  wire d_ff_1_q, or_1_out, or_2_out;
  wire [1:0] controlled_buffer_1_out;
  wire [6:0] register_1_q, register_2_q;

  or or_1 (or_1_out, AND, OR);
  assign controlled_buffer_1_out = AND ? 2'b10 : 2'bz;  // Controlled_Buffer controlled_buffer_1
  assign controlled_buffer_1_out = OR ? 2'b11 : 2'bz;  // Controlled_Buffer controlled_buffer_2
  or or_2 (or_2_out, OR, AND);
  D_Flip_Flop d_ff_1 (.clk(CLK), .D(or_1_out), .Q(d_ff_1_q));  // open: Qn, preset, en, reset
  Register #(.width(7)) register_1 (.D(in_2), .Q(register_1_q), .clk(d_ff_1_q));  // open: en, clr
  D_Flip_Flop d_ff_2 (.clk(CLK), .D(d_ff_1_q), .Q(DONE));  // open: Qn, preset, en, reset
  Register #(.width(7)) register_2 (.D(in_2), .Q(register_2_q), .clk(DONE));  // open: en, clr
  // Probe on RES[5:4]
  Register #(.width(2)) register_3 (.D(controlled_buffer_1_out), .Q(RES[7:6]), .clk(or_2_out));  // open: en, clr
  \дешифратор  \u_дешифратор_1  (.in_1(register_1_q), ._2_DIG(RES[5:4]));  // open: _4_DIG
  // Probe on RES[3:0]
  \дешифратор  \u_дешифратор_2  (.in_1(register_2_q), ._4_DIG(RES[3:0]));  // open: _2_DIG
endmodule
