// Logisim project Лаб1.circ as structural Verilog: 1 circuit, main circuit main
module main (
  input  A0,
  input  A1,
  input  A2,
  input  A3,
  output B0,
  output B1,
  output B2
);

  wire and_1_out, and_2_out, and_3_out, and_4_out, not_1_out, not_2_out, not_3_out, not_4_out, not_5_out;

  not not_1 (not_1_out, A0);
  and and_1 (and_1_out, not_1_out, A2);
  not not_2 (not_2_out, A0);
  and and_2 (and_2_out, not_2_out, A1);
  not not_3 (not_3_out, A0);
  not not_4 (not_4_out, A2);
  and and_3 (and_3_out, not_3_out, not_4_out, A3);
  not not_5 (not_5_out, A0);
  and and_4 (and_4_out, not_5_out, A1);
  or or_1 (B1, and_1_out, and_2_out);
  or or_2 (B2, and_3_out, and_4_out);

  assign B0 = A0;
endmodule
