// Logisim project 3 ЛАБА.circ as structural Verilog: 6 circuits, main circuit Half-Adder
module Half_Adder (
  input  A,
  input  B,
  output S,
  output COUT
);

  xor xor_1 (S, A, B);
  and and_1 (COUT, B, A);
endmodule

module Full_Adder (
  input  Cin,
  input  A,
  input  B,
  output S,
  output Cout
);

  wire half_adder_1_cout, half_adder_1_s, half_adder_2_cout;

  Half_Adder half_adder_1 (.A(A), .B(B), .S(half_adder_1_s), .COUT(half_adder_1_cout));
  Half_Adder half_adder_2 (.A(Cin), .B(half_adder_1_s), .S(S), .COUT(half_adder_2_cout));
  or or_1 (Cout, half_adder_2_cout, half_adder_1_cout);
endmodule

module Ripple_Carry_Adder (
  input  in_1,
  input  [7:0] A,
  input  [7:0] B,
  output Cout,
  output [7:0] S
);

  wire full_adder_2_cout, full_adder_3_cout, full_adder_4_cout, full_adder_5_cout, full_adder_6_cout,
       full_adder_7_cout, full_adder_8_cout;

  Full_Adder full_adder_1 (.Cin(full_adder_2_cout), .A(A[7]), .B(B[7]), .S(S[7]), .Cout(Cout));
  Full_Adder full_adder_2 (.Cin(full_adder_3_cout), .A(A[6]), .B(B[6]), .S(S[6]), .Cout(full_adder_2_cout));
  Full_Adder full_adder_3 (.Cin(full_adder_4_cout), .A(A[5]), .B(B[5]), .S(S[5]), .Cout(full_adder_3_cout));
  Full_Adder full_adder_4 (.Cin(full_adder_5_cout), .A(A[4]), .B(B[4]), .S(S[4]), .Cout(full_adder_4_cout));
  Full_Adder full_adder_5 (.Cin(full_adder_6_cout), .A(A[3]), .B(B[3]), .S(S[3]), .Cout(full_adder_5_cout));
  Full_Adder full_adder_6 (.Cin(full_adder_7_cout), .A(A[2]), .B(B[2]), .S(S[2]), .Cout(full_adder_6_cout));
  Full_Adder full_adder_7 (.Cin(full_adder_8_cout), .A(A[1]), .B(B[1]), .S(S[1]), .Cout(full_adder_7_cout));
  Full_Adder full_adder_8 (.Cin(in_1), .A(A[0]), .B(B[0]), .S(S[0]), .Cout(full_adder_8_cout));
endmodule

module Subtractor (
  input  [7:0] in_1,
  input  [7:0] in_2,
  input  in_3,
  output out_4,
  output [7:0] out_5
);

  wire ripple_carry_adder_1_cout;
  wire [7:0] invertor_1_out_3;

  xor xor_1 (out_4, ripple_carry_adder_1_cout, in_3);
  Ripple_Carry_Adder ripple_carry_adder_1 (
    .A(in_1), .B(invertor_1_out_3), .Cout(ripple_carry_adder_1_cout), .S(out_5), .in_1(in_3));
  Invertor invertor_1 (.in_2(in_3), .in_1(in_2), .out_3(invertor_1_out_3));
endmodule

module Multiplyer (
  input  A4,
  input  A3,
  input  A2,
  input  A1,
  input  B1,
  input  B2,
  input  B3,
  input  B4,
  output out_9,
  output out_10,
  output out_11,
  output out_12,
  output out_13,
  output out_14,
  output out_15,
  output out_16
);

  wire and_1_out, and_2_out, and_3_out, and_4_out, and_5_out, and_6_out, and_7_out, and_8_out, and_9_out,
       and_10_out, and_11_out, and_12_out, and_13_out, and_14_out, and_15_out, full_adder_2_cout,
       full_adder_2_s, full_adder_3_cout, full_adder_3_s, full_adder_4_cout, full_adder_5_cout,
       full_adder_5_s, full_adder_6_cout, full_adder_7_cout, full_adder_7_s, full_adder_8_cout,
       full_adder_8_s, full_adder_9_cout, full_adder_10_cout, full_adder_10_s, full_adder_11_cout,
       full_adder_12_cout;

  and and_1 (and_1_out, A4, B4);
  Full_Adder full_adder_1 (.Cin(full_adder_4_cout), .A(full_adder_3_cout), .B(and_1_out), .S(out_10), .Cout(out_9));
  and and_2 (and_2_out, A4, B2);
  Full_Adder full_adder_2 (
    .Cin(full_adder_7_cout), .A(and_2_out), .B(1'b0), .S(full_adder_2_s), .Cout(full_adder_2_cout));
  and and_3 (and_3_out, B3, A4);
  Full_Adder full_adder_3 (
    .Cin(full_adder_5_cout), .A(full_adder_2_cout), .B(and_3_out), .S(full_adder_3_s),
    .Cout(full_adder_3_cout));
  and and_4 (and_4_out, A3, B4);
  Full_Adder full_adder_4 (
    .Cin(full_adder_6_cout), .A(full_adder_3_s), .B(and_4_out), .S(out_11), .Cout(full_adder_4_cout));
  and and_5 (and_5_out, A3, B2);
  and and_6 (and_6_out, B3, A3);
  Full_Adder full_adder_5 (
    .Cin(full_adder_8_cout), .A(full_adder_2_s), .B(and_6_out), .S(full_adder_5_s), .Cout(full_adder_5_cout));
  and and_7 (and_7_out, A2, B4);
  Full_Adder full_adder_6 (
    .Cin(full_adder_9_cout), .A(full_adder_5_s), .B(and_7_out), .S(out_12), .Cout(full_adder_6_cout));
  and and_8 (and_8_out, A4, B1);
  and and_9 (and_9_out, A2, B2);
  Full_Adder full_adder_7 (
    .Cin(full_adder_10_cout), .A(and_5_out), .B(and_8_out), .S(full_adder_7_s), .Cout(full_adder_7_cout));
  and and_10 (and_10_out, B3, A2);
  Full_Adder full_adder_8 (
    .Cin(full_adder_11_cout), .A(full_adder_7_s), .B(and_10_out), .S(full_adder_8_s), .Cout(full_adder_8_cout));
  and and_11 (and_11_out, A1, B4);
  Full_Adder full_adder_9 (.Cin(1'b0), .A(full_adder_8_s), .B(and_11_out), .S(out_13), .Cout(full_adder_9_cout));
  and and_12 (and_12_out, A3, B1);
  Full_Adder full_adder_10 (
    .Cin(full_adder_12_cout), .A(and_9_out), .B(and_12_out), .S(full_adder_10_s), .Cout(full_adder_10_cout));
  and and_13 (and_13_out, B3, A1);
  Full_Adder full_adder_11 (.Cin(1'b0), .A(full_adder_10_s), .B(and_13_out), .S(out_14), .Cout(full_adder_11_cout));
  and and_14 (and_14_out, A2, B1);
  and and_15 (and_15_out, A1, B2);
  Full_Adder full_adder_12 (.Cin(1'b0), .A(and_15_out), .B(and_14_out), .S(out_15), .Cout(full_adder_12_cout));
  and and_16 (out_16, A1, B1);
endmodule

module Invertor (
  input  [7:0] in_1,
  input  in_2,
  output [7:0] out_3
);

  xor xor_1 (out_3[7], in_2, in_1[7]);
  xor xor_2 (out_3[6], in_2, in_1[6]);
  xor xor_3 (out_3[5], in_2, in_1[5]);
  xor xor_4 (out_3[3], in_2, in_1[3]);
  xor xor_5 (out_3[4], in_2, in_1[4]);
  xor xor_6 (out_3[1], in_2, in_1[1]);
  xor xor_7 (out_3[2], in_2, in_1[2]);
  xor xor_8 (out_3[0], in_2, in_1[0]);
endmodule
