// Logisim project 5 ЛАБА.circ as structural Verilog
module RS_flip_flop_out (
  input  RESET,
  input  SET,
  output Q,
  output Q_prime
);

  nor nor_1 (Q, RESET, Q_prime);
  nor nor_2 (Q_prime, Q, SET);
endmodule

module RS_flip_flop (
  input  RESET,
  input  Enable,
  input  SET,
  output Q,
  output Q_prime
);

  wire and_1_out, and_2_out;

  and and_1 (and_1_out, RESET, Enable);
  and and_2 (and_2_out, Enable, SET);
  nor nor_1 (Q, and_1_out, Q_prime);
  nor nor_2 (Q_prime, Q, and_2_out);
endmodule

module D_flip_flop_lvl (
  input  D,
  input  C,
  output Q,
  output Q_prime
);

  wire not_1_out;

  not not_1 (not_1_out, D);
  RS_flip_flop rs_flip_flop_1 (.RESET(not_1_out), .Enable(C), .SET(D), .Q(Q), .Q_prime(Q_prime));
endmodule

module D_flip_flop (
  input  D,
  input  C,
  output Q,
  output Q_prime
);

  wire d_flip_flop_lvl_1_q, not_1_out;

  D_flip_flop_lvl d_flip_flop_lvl_1 (.D(D), .C(C), .Q(d_flip_flop_lvl_1_q));  // open: Q_prime
  not not_1 (not_1_out, C);
  D_flip_flop_lvl d_flip_flop_lvl_2 (.D(d_flip_flop_lvl_1_q), .C(not_1_out), .Q(Q), .Q_prime(Q_prime));
endmodule

module _8_bit_Register (
  input  in_1,
  input  [7:0] in_2,
  output [7:0] out_3
);

  D_Flip_Flop d_ff_1 (.clk(in_1), .D(in_2[0]), .Q(out_3[0]));  // open: Qn, preset, en, reset
  D_Flip_Flop d_ff_2 (.clk(in_1), .D(in_2[1]), .Q(out_3[1]));  // open: Qn, preset, en, reset
  D_Flip_Flop d_ff_3 (.clk(in_1), .D(in_2[2]), .Q(out_3[2]));  // open: Qn, preset, en, reset
  D_Flip_Flop d_ff_4 (.clk(in_1), .D(in_2[3]), .Q(out_3[3]));  // open: Qn, preset, en, reset
  D_Flip_Flop d_ff_5 (.clk(in_1), .D(in_2[4]), .Q(out_3[4]));  // open: Qn, preset, en, reset
  D_Flip_Flop d_ff_6 (.clk(in_1), .D(in_2[5]), .Q(out_3[5]));  // open: Qn, preset, en, reset
  D_Flip_Flop d_ff_7 (.clk(in_1), .D(in_2[6]), .Q(out_3[6]));  // open: Qn, preset, en, reset
  D_Flip_Flop d_ff_8 (.clk(in_1), .D(in_2[7]), .Q(out_3[7]));  // open: Qn, preset, en, reset
endmodule

module _4_bit_register (
  input  in_1,
  output [3:0] out_2
);

  wire d_ff_1_qn, d_ff_2_qn, d_ff_3_qn, d_ff_4_qn;

  D_Flip_Flop d_ff_1 (.clk(in_1), .D(d_ff_1_qn), .Q(out_2[0]), .Qn(d_ff_1_qn));  // open: preset, en, reset
  D_Flip_Flop d_ff_2 (.clk(d_ff_1_qn), .D(d_ff_2_qn), .Q(out_2[1]), .Qn(d_ff_2_qn));  // open: preset, en, reset
  D_Flip_Flop d_ff_3 (.clk(d_ff_2_qn), .D(d_ff_3_qn), .Q(out_2[2]), .Qn(d_ff_3_qn));  // open: preset, en, reset
  D_Flip_Flop d_ff_4 (.clk(d_ff_3_qn), .D(d_ff_4_qn), .Q(out_2[3]), .Qn(d_ff_4_qn));  // open: preset, en, reset
endmodule

module Summator_With_Reg (
  input  [7:0] in_1,
  input  [7:0] in_2,
  input  in_3,
  input  in_4,
  output out_5,
  output [7:0] out_6
);

  wire [7:0] multiplexer_1_out, n8_bit_register_1_out_3;

  Multiplexer #(.width(8)) multiplexer_1 (
    .in0(in_2), .in1(n8_bit_register_1_out_3), .out(multiplexer_1_out), .sel(in_4), .en(1'b1));
  Ripple_Carry_Adder ripple_carry_adder_1 (.A(in_1), .B(multiplexer_1_out), .Cout(out_5), .S(out_6), .in_1(1'b0));
  _8_bit_Register u_8_bit_register_1 (.in_2(out_6), .out_3(n8_bit_register_1_out_3), .in_1(in_3));
endmodule

module Summator_mem (
  input  [7:0] in_1,
  input  in_2,
  input  in_3,
  output [7:0] out_4
);

  wire [7:0] ripple_carry_adder_1_s;

  Ripple_Carry_Adder ripple_carry_adder_1 (.A(in_1), .B(out_4), .S(ripple_carry_adder_1_s), .in_1(1'b0));  // open: Cout
  Register register_1 (.D(ripple_carry_adder_1_s), .Q(out_4), .clk(in_2), .clr(in_3));  // open: en
endmodule

module _64bit_mem (
  input  in_1,
  input  [7:0] in_2,
  input  [2:0] in_3,
  input  [2:0] in_4,
  input  in_5,
  output [7:0] out_6
);

  wire demultiplexer_2_out0, demultiplexer_2_out1, demultiplexer_2_out2, demultiplexer_2_out4,
       demultiplexer_2_out5, demultiplexer_2_out6, demultiplexer_2_out7;
  wire [7:0] demultiplexer_1_out0, demultiplexer_1_out1, demultiplexer_1_out2, demultiplexer_1_out3,
       demultiplexer_1_out4, demultiplexer_1_out5, demultiplexer_1_out6, demultiplexer_1_out7, register_1_q,
       register_2_q, register_3_q, register_4_q, register_5_q, register_6_q, register_7_q, register_8_q;

  Demultiplexer #(.select(3), .width(8)) demultiplexer_1 (
    .out0(demultiplexer_1_out0), .out1(demultiplexer_1_out1), .out2(demultiplexer_1_out2),
    .out3(demultiplexer_1_out3), .out4(demultiplexer_1_out4), .out5(demultiplexer_1_out5),
    .out6(demultiplexer_1_out6), .out7(demultiplexer_1_out7), .in(in_2), .sel(in_4));  // open: en
  Register register_1 (.D(demultiplexer_1_out0), .Q(register_1_q), .clk(demultiplexer_2_out0), .clr(in_1));  // open: en
  Register register_2 (.D(demultiplexer_1_out1), .Q(register_2_q), .clk(demultiplexer_2_out1), .clr(in_1));  // open: en
  Register register_3 (.D(demultiplexer_1_out2), .Q(register_3_q), .clk(demultiplexer_2_out2), .clr(in_1));  // open: en
  Register register_4 (.D(demultiplexer_1_out3), .Q(register_4_q), .clk(in_1), .clr(in_1));  // open: en
  Demultiplexer #(.select(3)) demultiplexer_2 (
    .out0(demultiplexer_2_out0), .out1(demultiplexer_2_out1), .out2(demultiplexer_2_out2), .out3(in_1),
    .out4(demultiplexer_2_out4), .out5(demultiplexer_2_out5), .out6(demultiplexer_2_out6),
    .out7(demultiplexer_2_out7), .in(in_5), .sel(in_4));  // open: en
  Register register_5 (.D(demultiplexer_1_out5), .Q(register_5_q), .clk(demultiplexer_2_out5), .clr(in_1));  // open: en
  Register register_6 (.D(demultiplexer_1_out4), .Q(register_6_q), .clk(demultiplexer_2_out4), .clr(in_1));  // open: en
  Register register_7 (.D(demultiplexer_1_out6), .Q(register_7_q), .clk(demultiplexer_2_out6), .clr(in_1));  // open: en
  Register register_8 (.D(demultiplexer_1_out7), .Q(register_8_q), .clk(demultiplexer_2_out7), .clr(in_1));  // open: en
  Multiplexer #(.select(3), .width(8)) multiplexer_1 (
    .in0(register_1_q), .in1(register_2_q), .in2(register_3_q), .in3(register_4_q), .in4(register_6_q),
    .in5(register_5_q), .in6(register_7_q), .in7(register_8_q), .out(out_6), .sel(in_3));  // open: en
endmodule
